# Fritzing sketch schematics (saved by Fritzing 0.9.4)
breadboards: 1

parts:
  Composant1 = Arduino Nano (Rev3.0)
  ENCODER1 = Rotary Encoder with Knob
  Composant2 = OLED Monochrome 128x32 I2C [part_number=931]
  J1 = Piezo Speaker

nets:
  GND: Composant1.GND, ENCODER1.no_name_yet#2, ENCODER1.no_name_yet#4, Composant2.GND, J1.pin1
  N1: Composant1.D2, ENCODER1.no_name_yet#3
  N2: Composant1.D3, ENCODER1.no_name_yet#1
  N3: Composant1.D4, ENCODER1.no_name_yet#5
  N4: Composant1.D8, J1.pin2
  5V: Composant1.5V, Composant2.VIN
  N5: Composant1.A5, Composant2.SCL
  N6: Composant1.A4, Composant2.SDA

custom parts:
  Rotary Encoder with Knob: Rotary Encoder with 1/4" Shaft and Knob
  OLED Monochrome 128x32 I2C: These displays are small, only about 1" diagonal, but very readable due to the high contrast of an OLED display. This display is made of 128x32 individual white OLED pixels, each one is turned on or off by the controller chip. Because the display makes its own light, no backlight is required. This reduces the power required to run the OLED and is why the display has such high contrast; we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
